// Logisim project SchemesForExam.circ as structural Verilog
module HS (
  input  A,
  input  B,
  output S,
  output C
);

  xor xor_1 (S, A, B);
  and and_1 (C, A, B);
endmodule

module FA (
  input  Cin,
  input  A,
  input  B,
  output S,
  output C
);

  wire hs_1_c, hs_1_s, hs_2_c;

  HS hs_1 (.A(A), .B(B), .S(hs_1_s), .C(hs_1_c));
  HS hs_2 (.A(Cin), .B(hs_1_s), .S(S), .C(hs_2_c));
  or or_1 (C, hs_2_c, hs_1_c);
endmodule

module CD_4_2 (
  input  D0,
  input  D1,
  input  D2,
  input  D3,
  output Y1,
  output Y0
);

  or or_1 (Y1, D2, D3);
  or or_2 (Y0, D1, D3);
endmodule

module CD_8_3 (
  input  D0,
  input  D1,
  input  D2,
  input  D3,
  input  D4,
  input  D5,
  input  D6,
  input  D7,
  output Y2,
  output Y1,
  output Y0
);

  or or_1 (Y2, D4, D5, D6, D7);
  or or_2 (Y1, D2, D3, D6, D7);
  or or_3 (Y0, D1, D3, D5, D7);
endmodule

module CD_8_3_P (
  input  D0,
  input  D1,
  input  D2,
  input  D3,
  input  D4,
  input  D5,
  input  D6,
  input  D7,
  output Y2,
  output Y1,
  output Y0,
  output V
);

  wire and_1_out, and_2_out, and_3_out, and_4_out, nand_1_out, nand_2_out, nor_1_out, not_1_out, or_2_out;

  or or_1 (Y2, D7, D6, D5, D4);
  nor nor_1 (nor_1_out, D5, D4);
  or or_2 (or_2_out, D3, D2);
  not not_1 (not_1_out, D6);
  nand nand_1 (nand_1_out, D6, D4);
  nand nand_2 (nand_2_out, D6, D4, D2);
  or or_3 (V, D7, D6, D5, D4, D3, D2, D1, D0);
  and and_1 (and_1_out, nor_1_out, or_2_out);
  and and_2 (and_2_out, not_1_out, D5);
  and and_3 (and_3_out, nand_1_out, D3);
  and and_4 (and_4_out, nand_2_out, D1);
  or or_4 (Y1, D7, D6, and_1_out);
  or or_5 (Y0, D7, and_2_out, and_3_out, and_4_out);
endmodule

module DC_2_4 (
  input  D1,
  input  D0,
  output Y0,
  output Y1,
  output Y2,
  output Y3
);

  wire not_1_out, not_2_out, not_3_out, not_4_out;

  not not_1 (not_1_out, D1);
  not not_2 (not_2_out, D0);
  not not_3 (not_3_out, D1);
  not not_4 (not_4_out, D0);
  and and_1 (Y3, D1, D0);
  and and_2 (Y0, not_1_out, not_2_out);
  and and_3 (Y1, not_3_out, D0);
  and and_4 (Y2, D1, not_4_out);
endmodule

module DC_3_8 (
  input  D2,
  input  D1,
  input  D0,
  output Y0,
  output Y1,
  output Y2,
  output Y3,
  output Y4,
  output Y5,
  output Y6,
  output Y7
);

  wire not_1_out, not_2_out, not_3_out, not_4_out, not_5_out, not_6_out, not_7_out, not_8_out, not_9_out,
       not_10_out, not_11_out, not_12_out;

  not not_1 (not_1_out, D2);
  not not_2 (not_2_out, D1);
  not not_3 (not_3_out, D0);
  not not_4 (not_4_out, D2);
  not not_5 (not_5_out, D1);
  not not_6 (not_6_out, D2);
  not not_7 (not_7_out, D0);
  not not_8 (not_8_out, D2);
  not not_9 (not_9_out, D1);
  not not_10 (not_10_out, D0);
  not not_11 (not_11_out, D1);
  not not_12 (not_12_out, D0);
  and and_1 (Y7, D2, D1, D0);
  and and_2 (Y0, not_1_out, not_2_out, not_3_out);
  and and_3 (Y1, not_4_out, not_5_out, D0);
  and and_4 (Y2, not_6_out, D1, not_7_out);
  and and_5 (Y3, not_8_out, D1, D0);
  and and_6 (Y4, D2, not_9_out, not_10_out);
  and and_7 (Y5, D2, not_11_out, D0);
  and and_8 (Y6, D2, D1, not_12_out);
endmodule

module MUX_4_1 (
  input  S1,
  input  S0,
  input  D0,
  input  D1,
  input  D2,
  input  D3,
  output Y
);

  wire and_1_out, and_2_out, and_3_out, and_4_out, not_1_out, not_2_out, not_3_out, not_4_out;

  not not_1 (not_1_out, S1);
  not not_2 (not_2_out, S0);
  not not_3 (not_3_out, S1);
  not not_4 (not_4_out, S0);
  and and_1 (and_1_out, not_1_out, not_2_out, D0);
  and and_2 (and_2_out, not_3_out, S0, D1);
  and and_3 (and_3_out, S1, not_4_out, D2);
  and and_4 (and_4_out, S1, S0, D3);
  or or_1 (Y, and_1_out, and_2_out, and_3_out, and_4_out);
endmodule

module DMX_1_4 (
  input  S1,
  input  S0,
  input  D,
  output Y0,
  output Y1,
  output Y2,
  output Y3
);

  wire not_1_out, not_2_out, not_3_out, not_4_out;

  not not_1 (not_1_out, S1);
  not not_2 (not_2_out, S0);
  not not_3 (not_3_out, S1);
  not not_4 (not_4_out, S0);
  and and_1 (Y3, S1, S0, D);
  and and_2 (Y0, not_1_out, not_2_out, D);
  and and_3 (Y1, not_3_out, S0, D);
  and and_4 (Y2, S1, not_4_out, D);
endmodule

module RS_Async (
  input  R,
  input  S,
  output Q,
  output nQ
);

  nor nor_1 (Q, R, nQ);
  nor nor_2 (nQ, Q, S);
endmodule

module RS_Sync (
  input  R,
  input  C,
  input  S,
  output Q,
  output nQ
);

  wire and_1_out, and_2_out;

  and and_1 (and_1_out, R, C);
  and and_2 (and_2_out, C, S);
  nor nor_1 (Q, and_1_out, nQ);
  nor nor_2 (nQ, Q, and_2_out);
endmodule

module D_1 (
  input  D,
  input  C,
  output Q,
  output nQ
);

  wire nand_1_out, nand_2_out;

  JK jk_1 ();  // open: Q, nQ, J, C, K
  nand nand_1 (nand_1_out, D, C);
  nand nand_2 (nand_2_out, nand_1_out, C);
  nand nand_3 (Q, nand_1_out, nQ);
  nand nand_4 (nQ, Q, nand_2_out);
endmodule

module D_2 (
  input  D,
  input  \С ,
  output Q,
  output nQ
);

  wire d_1_1_q, not_1_out;

  not not_1 (not_1_out, \С );
  D_1 d_1_1 (.D(D), .C(not_1_out), .Q(d_1_1_q));  // open: nQ
  D_1 d_1_2 (.D(d_1_1_q), .C(\С ), .Q(Q), .nQ(nQ));
endmodule

module JK (
  input  J,
  input  C,
  input  K,
  output Q,
  output nQ
);

  wire nand_1_out, nand_2_out;

  nand nand_1 (nand_1_out, nQ, J, C);
  nand nand_2 (nand_2_out, C, K, Q);
  nand nand_3 (Q, nand_1_out, nQ);
  nand nand_4 (nQ, Q, nand_2_out);
endmodule

module DMUX_16_1 (
  input  D,
  input  S0,
  input  S1,
  input  S2,
  input  S3,
  output Y0,
  output Y1,
  output Y2,
  output Y3,
  output Y4,
  output Y5,
  output Y6,
  output Y7,
  output Y8,
  output Y9,
  output Y10,
  output Y11
);

  wire not_1_out, not_2_out, not_3_out, not_4_out, not_5_out, not_6_out, not_7_out, not_8_out, not_9_out,
       not_10_out, not_11_out, not_12_out, not_13_out, not_14_out, not_15_out, not_16_out, not_17_out,
       not_18_out, not_19_out, not_20_out, not_21_out, not_22_out, not_23_out, not_24_out, not_25_out,
       not_26_out, not_27_out, not_28_out, not_29_out, not_30_out, not_31_out, not_32_out, not_33_out,
       not_34_out, not_35_out, not_36_out, not_37_out, not_38_out, not_39_out, not_40_out;

  not not_1 (not_1_out, D);
  not not_2 (not_2_out, S0);
  not not_3 (not_3_out, S1);
  not not_4 (not_4_out, S2);
  not not_5 (not_5_out, S3);
  not not_6 (not_6_out, D);
  not not_7 (not_7_out, S0);
  not not_8 (not_8_out, S1);
  not not_9 (not_9_out, S2);
  not not_10 (not_10_out, D);
  not not_11 (not_11_out, S0);
  not not_12 (not_12_out, S1);
  not not_13 (not_13_out, S3);
  not not_14 (not_14_out, D);
  not not_15 (not_15_out, S0);
  not not_16 (not_16_out, S1);
  not not_17 (not_17_out, D);
  not not_18 (not_18_out, S0);
  not not_19 (not_19_out, S2);
  not not_20 (not_20_out, S3);
  not not_21 (not_21_out, D);
  not not_22 (not_22_out, S0);
  not not_23 (not_23_out, S2);
  not not_24 (not_24_out, D);
  not not_25 (not_25_out, S0);
  not not_26 (not_26_out, S3);
  not not_27 (not_27_out, D);
  not not_28 (not_28_out, S0);
  not not_29 (not_29_out, D);
  not not_30 (not_30_out, S1);
  not not_31 (not_31_out, S2);
  not not_32 (not_32_out, S3);
  not not_33 (not_33_out, D);
  not not_34 (not_34_out, S1);
  not not_35 (not_35_out, S2);
  not not_36 (not_36_out, D);
  not not_37 (not_37_out, S1);
  not not_38 (not_38_out, S3);
  not not_39 (not_39_out, D);
  not not_40 (not_40_out, S1);
  and and_1 (Y0, not_1_out, not_2_out, not_3_out, not_4_out, not_5_out);
  and and_2 (Y1, not_6_out, not_7_out, not_8_out, not_9_out, S3);
  and and_3 (Y2, not_10_out, not_11_out, not_12_out, S2, not_13_out);
  and and_4 (Y3, not_14_out, not_15_out, not_16_out, S2, S3);
  and and_5 (Y4, not_17_out, not_18_out, S1, not_19_out, not_20_out);
  and and_6 (Y5, not_21_out, not_22_out, S1, not_23_out, S3);
  and and_7 (Y6, not_24_out, not_25_out, S1, S2, not_26_out);
  and and_8 (Y7, not_27_out, not_28_out, S1, S2, S3);
  and and_9 (Y8, not_29_out, S0, not_30_out, not_31_out, not_32_out);
  and and_10 (Y9, not_33_out, S0, not_34_out, not_35_out, S3);
  and and_11 (Y10, not_36_out, S0, not_37_out, S2, not_38_out);
  and and_12 (Y11, not_39_out, S0, not_40_out, S2, S3);
endmodule
