// Logisim project BST_2502_Kochkin_lab1_task2.circ as structural Verilog: 2 circuits, main circuit main
module main (
  input  a,
  input  b,
  input  c,
  output y
);

  wire and_1_out, and_2_out, and_3_out, not_1_out, or_1_out;

  and and_1 (and_1_out, a, b);
  and and_2 (and_2_out, b, c);
  or or_1 (or_1_out, and_1_out, and_2_out);
  and and_3 (and_3_out, a, c);
  not not_1 (not_1_out, or_1_out);
  or or_2 (y, not_1_out, and_3_out);
endmodule

module main_basis (
  input  a,
  input  b,
  input  c,
  output y
);

  wire and_1_out, and_2_out, and_3_out, and_4_out, and_5_out, not_1_out, not_2_out, not_3_out, not_4_out;

  and and_1 (and_1_out, a, b);
  and and_2 (and_2_out, b, c);
  not not_1 (not_1_out, and_1_out);
  and and_3 (and_3_out, not_1_out, not_2_out);
  not not_2 (not_2_out, and_2_out);
  and and_4 (and_4_out, a, c);
  not not_3 (not_3_out, and_3_out);
  and and_5 (and_5_out, not_3_out, not_4_out);
  not not_4 (not_4_out, and_4_out);
  not not_5 (y, and_5_out);
endmodule
