// Logisim project BST_2502_Kochkin_lab1_task3.circ as structural Verilog: 1 circuit, main circuit main
module main (
  input  x1,
  input  x2,
  input  x3,
  output y1,
  output y2
);

  wire nand_1_out, not_1_out, not_2_out, not_3_out, or_1_out;

  not not_1 (not_1_out, x1);
  not not_2 (not_2_out, x2);
  or or_1 (or_1_out, not_1_out, not_2_out);
  not not_3 (not_3_out, x3);
  and and_1 (y2, x1, nand_1_out);
  nand nand_1 (nand_1_out, x2, x3);
  or or_2 (y1, or_1_out, not_3_out);
endmodule
