// Logisim project BST_2502_Kochkin_lab2_task1.circ as structural Verilog: 2 circuits, main circuit main
module main (
  input  x1,
  input  x2,
  input  x3,
  input  x4,
  output f
);

  wire and_1_out, and_2_out, and_3_out, and_4_out, nand_1_out, nand_2_out, not_1_out, not_2_out, or_1_out,
       or_2_out;

  nand nand_1 (nand_1_out, x1, x4);
  not not_1 (not_1_out, x1);
  not not_2 (not_2_out, x2);
  and and_1 (and_1_out, x1, x4);
  or or_1 (or_1_out, nand_1_out, x3);
  and and_2 (and_2_out, not_1_out, not_2_out);
  and and_3 (and_3_out, and_1_out, or_1_out);
  or or_2 (or_2_out, and_3_out, and_4_out);
  and and_4 (and_4_out, and_2_out, x3);
  nand nand_2 (nand_2_out, x1, x4);
  or or_3 (f, or_2_out, nand_2_out);
endmodule

module Karnaugh (
  input  x1,
  input  x2,
  input  x3,
  input  x4,
  output f
);

  wire and_1_out, and_2_out, and_3_out, and_4_out, nand_1_out, nand_2_out, not_1_out, not_2_out, or_1_out,
       or_2_out;

  nand nand_1 (nand_1_out, x1, x4);
  not not_1 (not_1_out, x1);
  not not_2 (not_2_out, x2);
  and and_1 (and_1_out, x1, x4);
  or or_1 (or_1_out, nand_1_out, x3);
  and and_2 (and_2_out, not_1_out, not_2_out);
  and and_3 (and_3_out, and_1_out, or_1_out);
  or or_2 (or_2_out, and_3_out, and_4_out);
  and and_4 (and_4_out, and_2_out, x3);
  nand nand_2 (nand_2_out, x1, x4);
  or or_3 (f, or_2_out, nand_2_out);
endmodule
