// Logisim project BST_2502_Kochkin_lab3.circ as structural Verilog: 3 circuits, main circuit Задание 1
module \Задание_1  (
  input  x0,
  input  x1,
  input  x2,
  input  x3,
  input  x4,
  input  x5,
  input  x6,
  input  x7,
  output y1,
  output y2,
  output y3
);

  or or_1 (y1, x1, x3, x5, x7);
  or or_2 (y2, x2, x3, x6, x7);
  or or_3 (y3, x4, x5, x6, x7);
endmodule

module \Задание_2  (
  input  x0,
  input  x1,
  input  x2,
  input  x3,
  input  x4,
  input  x5,
  input  x6,
  input  x7,
  output y1,
  output y2,
  output y3
);

  or or_1 (y1, x5, x4, x2, x1);
  or or_2 (y2, x6, x4, x0, x1);
  or or_3 (y3, x3, x2, x0, x1);
endmodule

module \Задание_3  (
  input  x0,
  input  x1,
  input  x2,
  input  x3,
  input  x4,
  input  x5,
  input  x6,
  input  x7,
  input  x8,
  input  x9,
  input  x10,
  input  x11,
  input  x12,
  input  x13,
  input  x14,
  input  x15,
  output y0,
  output y1,
  output y2,
  output y3
);

  or or_1 (y1, x12, x4, x5, x14, x6, x7, x15);
  or or_2 (y0, x12, x8, x10, x11, x14, x15);
  or or_3 (y2, x14, x2, x3, x6, x7, x10, x11, x15);
  or or_4 (y3, x1, x3, x5, x7, x11, x15);
endmodule
