// Logisim project BST_2502_Kochkin_lab3_task1.circ as structural Verilog: 1 circuit, main circuit main
module main (
  input  x0,
  input  x1,
  input  x2,
  input  x3,
  input  x4,
  input  x5,
  input  x6,
  input  x7,
  output y1,
  output y2,
  output y3
);

  or or_1 (y1, x1, x4, x7, x2);
  or or_2 (y2, x5, x4, x6, x2);
  or or_3 (y3, x0, x7, x6, x2);
endmodule
