// Logisim project BST_2502_Kochkin_lab3_task2.circ as structural Verilog: 1 circuit, main circuit main
module main (
  input  x0,
  input  x1,
  input  x2,
  input  x3,
  input  x4,
  input  x5,
  input  x6,
  input  x7,
  output y1,
  output y2,
  output y3
);

  or or_1 (y1, x5, x4, x2, x1);
  or or_2 (y2, x6, x4, x0, x1);
  or or_3 (y3, x3, x2, x0, x1);
endmodule
