// Logisim project BST_2502_Kochkin_lab3_task3.circ as structural Verilog: 1 circuit, main circuit main
module main (
  input  x0,
  input  x1,
  input  x2,
  input  x3,
  input  x4,
  input  x5,
  input  x6,
  input  x7,
  input  x8,
  input  x9,
  input  x10,
  input  x11,
  input  x12,
  input  x13,
  input  x14,
  input  x15,
  output y0,
  output y1,
  output y2,
  output y3
);

  or or_1 (y0, x8, x10, x11, x12, x14, x15);
  or or_2 (y1, x4, x5, x6, x7, x12, x14, x15);
  or or_3 (y2, x2, x3, x6, x8, x10, x11, x14, x15);
  or or_4 (y3, x1, x3, x5, x8, x11, x15);
endmodule
