// Logisim project BST_2502_Kochkin_lab4_task1.circ as structural Verilog: 1 circuit, main circuit main
module main (
  input  x3,
  input  x2,
  input  x1,
  output y0,
  output y1,
  output y2,
  output y3,
  output y4,
  output y5,
  output y6,
  output y7
);

  wire not_1_out, not_2_out, not_3_out, not_4_out, not_5_out, not_6_out, not_7_out, not_8_out, not_9_out,
       not_10_out, not_11_out, not_12_out;

  not not_1 (not_1_out, x1);
  not not_2 (not_2_out, x2);
  not not_3 (not_3_out, x3);
  not not_4 (not_4_out, x3);
  not not_5 (not_5_out, x2);
  not not_6 (not_6_out, x1);
  not not_7 (not_7_out, x3);
  not not_8 (not_8_out, x3);
  not not_9 (not_9_out, x2);
  not not_10 (not_10_out, x1);
  not not_11 (not_11_out, x2);
  not not_12 (not_12_out, x1);
  and and_1 (y7, x3, x2, x1);
  and and_2 (y0, not_1_out, not_2_out, not_3_out);
  and and_3 (y1, not_4_out, not_5_out, x1);
  and and_4 (y2, not_6_out, x2, not_7_out);
  and and_5 (y3, not_8_out, x2, x1);
  and and_6 (y4, x3, not_9_out, not_10_out);
  and and_7 (y5, x1, not_11_out, x3);
  and and_8 (y6, x3, x2, not_12_out);
endmodule
