// Logisim project BST_2502_Kochkin_lab4_task2.circ as structural Verilog: 1 circuit, main circuit main
module main (
  input  x3,
  input  x2,
  input  x1,
  output y0,
  output y1,
  output y2,
  output y3,
  output y4,
  output y5,
  output y6,
  output y7
);

  wire and_1_out, and_2_out, and_5_out, and_6_out, and_7_out, and_8_out, and_9_out, and_10_out, not_1_out,
       not_2_out, not_3_out, not_4_out, not_5_out, not_6_out, not_7_out, not_8_out, not_9_out, not_10_out,
       not_11_out, not_12_out, not_13_out;

  and and_1 (and_1_out, x3, x2);
  not not_1 (not_1_out, x1);
  and and_2 (and_2_out, x3, x2);
  not not_2 (not_2_out, x2);
  not not_3 (not_3_out, x2);
  not not_4 (not_4_out, x2);
  not not_5 (not_5_out, x3);
  not not_6 (not_6_out, x2);
  not not_7 (not_7_out, x3);
  not not_8 (not_8_out, x3);
  not not_9 (not_9_out, x2);
  and and_3 (y0, and_1_out, not_1_out);
  and and_4 (y1, and_2_out, x1);
  and and_5 (and_5_out, x3, not_2_out);
  and and_6 (and_6_out, x3, not_3_out);
  not not_10 (not_10_out, x1);
  and and_7 (and_7_out, x3, not_4_out);
  not not_11 (not_11_out, x1);
  and and_8 (and_8_out, not_5_out, not_6_out);
  and and_9 (and_9_out, not_7_out, x2);
  not not_12 (not_12_out, x1);
  and and_10 (and_10_out, not_8_out, not_9_out);
  not not_13 (not_13_out, x1);
  and and_11 (y2, and_5_out, x1);
  and and_12 (y3, and_6_out, not_10_out);
  and and_13 (y4, and_7_out, not_11_out);
  and and_14 (y5, and_8_out, x1);
  and and_15 (y6, and_9_out, not_12_out);
  and and_16 (y7, and_10_out, not_13_out);
endmodule
