// Logisim project BST_2502_Kochkin_lab5.circ as structural Verilog: 2 circuits, main circuit Задание 1
module \Задание_1  (
  input  x0,
  input  x1,
  input  x2,
  input  x3,
  output y
);

  wire D0_out, D1_out, D2_out, D3_out, D4_out, D5_out, D6_out, D7_out, D8_out, D9_out, D10_out, D11_out,
       D12_out, D13_out, D14_out, D15_out, not_1_out, not_2_out, not_3_out, not_4_out, not_5_out, not_6_out,
       not_7_out, not_8_out, not_9_out, not_10_out, not_11_out, not_12_out, not_13_out, not_14_out,
       not_15_out, not_16_out, not_17_out, not_18_out, not_19_out, not_20_out, not_21_out, not_22_out,
       not_23_out, not_24_out, not_25_out, not_26_out, not_27_out, not_28_out, not_29_out, not_30_out,
       not_31_out, not_32_out;

  not not_1 (not_1_out, x0);
  not not_2 (not_2_out, x1);
  not not_3 (not_3_out, x2);
  not not_4 (not_4_out, x3);
  not not_5 (not_5_out, x0);
  not not_6 (not_6_out, x1);
  not not_7 (not_7_out, x2);
  not not_8 (not_8_out, x0);
  not not_9 (not_9_out, x1);
  not not_10 (not_10_out, x3);
  not not_11 (not_11_out, x0);
  not not_12 (not_12_out, x1);
  not not_13 (not_13_out, x0);
  not not_14 (not_14_out, x2);
  not not_15 (not_15_out, x3);
  not not_16 (not_16_out, x0);
  not not_17 (not_17_out, x2);
  not not_18 (not_18_out, x0);
  not not_19 (not_19_out, x3);
  not not_20 (not_20_out, x0);
  not not_21 (not_21_out, x1);
  not not_22 (not_22_out, x2);
  not not_23 (not_23_out, x3);
  not not_24 (not_24_out, x1);
  not not_25 (not_25_out, x2);
  not not_26 (not_26_out, x1);
  not not_27 (not_27_out, x3);
  not not_28 (not_28_out, x1);
  not not_29 (not_29_out, x2);
  not not_30 (not_30_out, x3);
  not not_31 (not_31_out, x2);
  not not_32 (not_32_out, x3);
  and D0 (D0_out, not_1_out, not_2_out, not_3_out, not_4_out, 1'b1);
  and D1 (D1_out, not_5_out, not_6_out, not_7_out, x3, 1'b1);
  and D2 (D2_out, not_8_out, not_9_out, x2, not_10_out, 1'b0);
  and D3 (D3_out, not_11_out, not_12_out, x2, x3, 1'b0);
  and D4 (D4_out, not_13_out, x1, not_14_out, not_15_out, 1'b1);
  and D5 (D5_out, not_16_out, x1, not_17_out, x3, 1'b0);
  and D6 (D6_out, not_18_out, x1, x2, not_19_out, 1'b1);
  and D7 (D7_out, not_20_out, x1, x2, x3, 1'b1);
  and D8 (D8_out, x0, not_21_out, not_22_out, not_23_out, 1'b0);
  and D9 (D9_out, x0, not_24_out, not_25_out, x3, 1'b0);
  and D10 (D10_out, x0, not_26_out, x2, not_27_out, 1'b1);
  and D11 (D11_out, x0, not_28_out, x2, x3, 1'b0);
  and D12 (D12_out, x0, x1, not_29_out, not_30_out, 1'b0);
  and D13 (D13_out, x0, x1, not_31_out, x3, 1'b1);
  and D14 (D14_out, x0, x1, x2, not_32_out, 1'b0);
  and D15 (D15_out, x0, x1, x2, x3, 1'b1);
  or or_1 (y, D0_out, D1_out, D2_out, D3_out, D4_out, D5_out, D6_out, D7_out, D8_out, D9_out, D10_out, D11_out, D12_out, D13_out, D14_out, D15_out);
endmodule

module \Задание_2  (
  input  x0,
  input  x1,
  input  x2,
  input  x3,
  output Y0,
  output Y1,
  output Y2,
  output Y3,
  output Y4,
  output Y5,
  output Y6,
  output Y7,
  output Y8,
  output Y9,
  output Y10,
  output Y11,
  output Y12,
  output Y13,
  output Y14,
  output Y15
);

  wire not_1_out, not_2_out, not_3_out, not_4_out, not_5_out, not_6_out, not_7_out, not_8_out, not_9_out,
       not_10_out, not_11_out, not_12_out, not_13_out, not_14_out, not_15_out, not_16_out, not_17_out,
       not_18_out, not_19_out, not_20_out, not_21_out, not_22_out, not_23_out, not_24_out, not_25_out,
       not_26_out, not_27_out, not_28_out, not_29_out, not_30_out, not_31_out, not_32_out;

  not not_1 (not_1_out, x3);
  not not_2 (not_2_out, x2);
  not not_3 (not_3_out, x1);
  not not_4 (not_4_out, x0);
  not not_5 (not_5_out, x3);
  not not_6 (not_6_out, x2);
  not not_7 (not_7_out, x1);
  not not_8 (not_8_out, x3);
  not not_9 (not_9_out, x2);
  not not_10 (not_10_out, x0);
  not not_11 (not_11_out, x3);
  not not_12 (not_12_out, x2);
  not not_13 (not_13_out, x3);
  not not_14 (not_14_out, x1);
  not not_15 (not_15_out, x0);
  not not_16 (not_16_out, x3);
  not not_17 (not_17_out, x1);
  not not_18 (not_18_out, x3);
  not not_19 (not_19_out, x0);
  not not_20 (not_20_out, x3);
  not not_21 (not_21_out, x2);
  not not_22 (not_22_out, x1);
  not not_23 (not_23_out, x0);
  not not_24 (not_24_out, x2);
  not not_25 (not_25_out, x1);
  not not_26 (not_26_out, x2);
  not not_27 (not_27_out, x0);
  not not_28 (not_28_out, x2);
  not not_29 (not_29_out, x0);
  not not_30 (not_30_out, x1);
  not not_31 (not_31_out, x1);
  not not_32 (not_32_out, x0);
  and and_1 (Y0, not_1_out, not_2_out, not_3_out, not_4_out, 1'b1);
  and and_2 (Y1, not_5_out, not_6_out, not_7_out, x0, 1'b1);
  and and_3 (Y2, not_8_out, not_9_out, x1, not_10_out, 1'b0);
  and and_4 (Y3, not_11_out, not_12_out, x1, x0, 1'b0);
  and and_5 (Y4, not_13_out, x2, not_14_out, not_15_out, 1'b1);
  and and_6 (Y5, not_16_out, x2, not_17_out, x0, 1'b0);
  and and_7 (Y6, not_18_out, x2, x1, not_19_out, 1'b1);
  and and_8 (Y7, not_20_out, x2, x1, x0, 1'b1);
  and and_9 (Y8, x3, not_21_out, not_22_out, not_23_out, 1'b0);
  and and_10 (Y9, x3, not_24_out, not_25_out, x0, 1'b0);
  and and_11 (Y10, x3, not_26_out, x1, not_27_out, 1'b1);
  and and_12 (Y11, x3, not_28_out, x1, x0, 1'b0);
  and and_13 (Y12, not_29_out, x2, x3, not_30_out, 1'b0);
  and and_14 (Y13, x0, not_31_out, x2, x3, 1'b1);
  and and_15 (Y14, not_32_out, x1, x2, x3, 1'b0);
  and and_16 (Y15, x3, x2, x1, x0, 1'b1);
endmodule
