// Logisim project BST_2502_Kochkin_lab6.circ as structural Verilog
module RS_ASYNC_NOR (
  input  R,
  input  S,
  output Q,
  output nQ
);

  nor nor_1 (Q, R, nQ);
  nor nor_2 (nQ, Q, S);
endmodule

module RS_SYNC_NAND (
  input  S,
  input  C,
  input  R,
  output Q,
  output nQ
);

  wire and_1_out, and_2_out, not_1_out, not_2_out;

  not not_1 (not_1_out, S);
  and and_1 (and_1_out, not_1_out, C);
  and and_2 (and_2_out, C, not_2_out);
  not not_2 (not_2_out, R);
  nand nand_1 (Q, and_1_out, nQ);
  nand nand_2 (nQ, Q, and_2_out);
endmodule

module D_latch (
  input  CLK,
  input  D,
  output Q,
  output nQ
);

  wire and_1_out, and_2_out, not_1_out;

  and and_1 (and_1_out, CLK, not_1_out);
  not not_1 (not_1_out, D);
  and and_2 (and_2_out, CLK, D);
  RS_ASYNC_NOR rs_async_nor_1 (.R(and_1_out), .S(and_2_out), .Q(Q), .nQ(nQ));
endmodule

// D
module D_Trigger (
  input  CLK,
  input  D,
  output Q,
  output nQ
);

  wire d_latch_1_q, not_1_out;

  not not_1 (not_1_out, CLK);
  D_latch d_latch_1 (.CLK(not_1_out), .D(D), .Q(d_latch_1_q));  // open: nQ
  D_latch d_latch_2 (.CLK(CLK), .D(d_latch_1_q), .Q(Q), .nQ(nQ));

  // Notes on the sheet:
  //   L1
  //   L2
endmodule

// JK
module JK_Trigger (
  input  J,
  input  C,
  input  J_2,
  output Q,
  output nQ
);

  wire nand_1_out, nand_2_out;

  nand nand_1 (nand_1_out, J, C, nQ);
  nand nand_2 (nand_2_out, Q, C, J_2);
  nand nand_3 (Q, nand_1_out, nQ);
  nand nand_4 (nQ, Q, nand_2_out);
endmodule

module T_Trigger (
  input  in_1,
  input  in_2,
  output Q,
  output nQ
);

  wire nand_1_out, nand_2_out, nand_3_out, nand_4_out, nand_5_out, nand_6_out;

  nand nand_1 (nand_1_out, nQ, in_1, in_2);
  nand nand_2 (nand_2_out, in_2, in_1, Q);
  nand nand_3 (nand_3_out, nand_1_out, nand_4_out);
  nand nand_4 (nand_4_out, nand_1_out, nand_5_out);
  nand nand_5 (nand_5_out, nand_4_out, nand_2_out);
  nand nand_6 (nand_6_out, nand_5_out, nand_2_out);
  nand nand_7 (Q, nand_3_out, nQ);
  nand nand_8 (nQ, Q, nand_6_out);
endmodule
